# Fritzing sketch biruta (saved by Fritzing 0.9.3b)
breadboards: 2

parts:
  Componente1 = Arduino Uno (Rev3)
  S1 = Reed switch [package=THT]
  R1 = Resistor [tolerance=±5% resistance=4.7k package=THT]
  R2 = Resistor [tolerance=±5% resistance=10k package=THT]
  S2 = Reed switch [package=THT]
  R3 = Resistor [tolerance=±5% resistance=20k package=THT]
  S3 = Reed switch [package=THT]
  R4 = Resistor [tolerance=±5% resistance=40k package=THT]
  S4 = Reed switch [package=THT]
  R5 = Resistor [tolerance=±5% resistance=30k package=THT]
  S5 = Reed switch [package=THT]
  R6 = Resistor [tolerance=±5% resistance=50k package=THT]
  S6 = Reed switch [package=THT]
  R7 = Resistor [tolerance=±5% resistance=60k package=THT]
  S7 = Reed switch [package=THT]
  R8 = Resistor [tolerance=±5% resistance=70k package=THT]
  S8 = Reed switch [package=THT]
  R9 = Resistor [tolerance=±5% resistance=80k package=THT]

nets:
  N1: Componente1.A0, R1.Pin_0, R2.Pin_0, R3.Pin_0, R4.Pin_0, R5.Pin_0, R6.Pin_0, R7.Pin_0, R8.Pin_0, R9.Pin_0
  N2: Componente1.5V, S1.pin_1, S2.pin_1, S3.pin_1, S4.pin_1, S5.pin_1, S6.pin_1, S7.pin_1, S8.pin_1
  N3: Componente1.GND, R1.Pin_1
  N4: S1.pin_2, R2.Pin_1
  N5: S2.pin_2, R3.Pin_1
  N6: S3.pin_2, R4.Pin_1
  N7: S4.pin_2, R5.Pin_1
  N8: S5.pin_2, R6.Pin_1
  N9: S6.pin_2, R7.Pin_1
  N10: S7.pin_2, R8.Pin_1
  N11: S8.pin_2, R9.Pin_1
