# Fritzing sketch dht11 (saved by Fritzing 0.9.3b)

parts:
  Componente1 = Arduino Uno (Rev3) - ICSP
  RHT1 = Humidity and Temperature Sensor RHT03
  R1 = Resistor [tolerance=±5% resistance=5k package="0402 [SMD]"]

nets:
  N1: Componente1.GND, RHT1.GND_2
  N2: Componente1.D3_PWM, RHT1.Data-signal, R1.Pin_0
  5V: Componente1.5V, RHT1.Vcc, R1.Pin_1
