# Fritzing sketch ds18b20 (saved by Fritzing 0.9.3b)

parts:
  DS1 = DS18B20 1-Wire Temperature Sensor [part_number=DS18B20]
  Componente1 = Arduino Uno (Rev3) - ICSP
  R1 = Resistor [tolerance=±5% resistance=4.7k package="0805 [SMD]"]

nets:
  GND: DS1.GND, Componente1.GND
  N1: DS1.DQ, Componente1.D4, R1.Pin_1
  VDD: DS1.VDD, Componente1.5V, R1.Pin_0
