# Fritzing sketch fases_energia (saved by Fritzing 0.9.3b)
breadboards: 1

parts:
  R1 = Resistor [tolerance=±5% resistance=10k package="2512 [SMD]"]
  R2 = Resistor [tolerance=±5% resistance=820 package="2512 [SMD]"]
  U1 = Sharp PC817 [package=THT]
  X1 = USB Connectors [package=usb-microb]
  Arduino_Uno = Arduino Uno (Rev3)
  J1 = female pin header, 1 pin [form="♀ (female)"]
  R3 = Resistor [tolerance=±5% resistance=10k package="2512 [SMD]"]
  R4 = Resistor [tolerance=±5% resistance=820 package="2512 [SMD]"]
  U2 = Sharp PC817 [package=THT]
  X2 = USB Connectors [package=usb-microb]

nets:
  N1: R1.Pin_0, U1.Pin_3, Arduino_Uno.D2
  N2: R1.Pin_1, Arduino_Uno.GND, R3.Pin_1
  N3: R2.Pin_0, X1.VBUS
  N4: R2.Pin_1, U1.Pin_1
  N5: U1.Pin_2, X1.GND
  N6: U1.Pin_4, Arduino_Uno.5V, U2.Pin_4
  N7: Arduino_Uno.D3_PWM, R3.Pin_0, U2.Pin_3
  N8: Arduino_Uno.D4, J1.pin1
  N9: R4.Pin_0, X2.VBUS
  N10: R4.Pin_1, U2.Pin_1
  N11: U2.Pin_2, X2.GND

notes:
  Relé
