# Fritzing sketch pluviometro_anemometro (saved by Fritzing 0.9.3b)
breadboards: 1

parts:
  S1 = Reed switch [package=THT]
  Componente1 = Arduino Uno (Rev3)
  R1 = Resistor [tolerance=±5% resistance=10k package=THT]

nets:
  N1: S1.pin_1, Componente1.5V
  N2: S1.pin_2, Componente1.D3_PWM, R1.Pin_0
  N3: Componente1.GND, R1.Pin_1
