# Fritzing sketch regulador_tensao (saved by Fritzing 0.9.3b)
breadboards: 1

parts:
  C1 = Electrolytic Capacitor [capacitance=100µF package="100 mil [THT, electrolytic]"]
  C2 = Electrolytic Capacitor [capacitance=100µF package="100 mil [THT, electrolytic]"]
  U1 = Voltage Regulator - 5V [package="TO220 [THT]"]
  J1 = Screw terminal - 2 pins [package=THT]
  J2 = Screw terminal - 2 pins [package=THT]

nets:
  N1: C1.-, C2.-, U1.GND, J1.pin2, J2.pin1
  N2: C1.+, U1.input_voltage, J1.pin1
  N3: C2.+, U1.output_voltage, J2.pin2

notes:
  12V
  9V
